# Fritzing sketch DiagramPowerSupply (saved by Fritzing 0.8.7b)
circuit board: 10.1315cm x 6.12799cm
breadboards: 1

parts:
  7805 = Voltage Regulator - 5V [package="TO220 [THT]"]
  D1 = Diode [package=diode-1n4001]
  D2 = Diode [package=diode-1n4001]
  D3 = Diode [package=diode-1n4001]
  D4 = Diode [package=diode-1n4001]
  AC = Header 1 [package=1x01_offset]
  AC_2 = Header 1 [package=1x01_offset]
  0_1uF = Ceramic Capacitor [capacitance=100nF package="100 mil [THT, multilayer]"]
  0_1uF_2 = Ceramic Capacitor [capacitance=100nF package="100 mil [THT, multilayer]"]
  +5V = Header 1 [package=1x01_offset]
  GND = Header 1 [package=1x01_offset]
  470uF = Electrolytic Capacitor [capacitance=0.47mF package="100 mil [THT, electrolytic]"]

nets:
  N1: 7805.input_voltage, D2.C, D4.C, 0_1uF_2.1, 470uF.+
  N2: 7805.GND, D1.A, D3.A, 0_1uF.0, 0_1uF_2.0, GND.1, 470uF.-
  N3: 7805.output_voltage, 0_1uF.1, +5V.1
  N4: D1.C, D4.A, AC.1
  N5: D2.A, D3.C, AC_2.1
