# Fritzing sketch DiagramSeg (saved by Fritzing 0.8.7b)
circuit board: 8.46667cm x 5.64444cm
breadboards: 1

parts:
  ATMega328p = atmega328 [package=dip]
  470 = Resistor [tolerance=±5% resistance=470 package=THT]
  470_2 = Resistor [tolerance=±5% resistance=470 package=THT]
  470_3 = Resistor [tolerance=±5% resistance=470 package=THT]
  470_4 = Resistor [tolerance=±5% resistance=470 package=THT]
  10k = Resistor [tolerance=±5% resistance=10k package=THT]
  7SEG = 7-SEGMENT-4DIGIT-YOUNGSUN [package=7-segment-4digit-youngsun]
  11 = Header 1 [package=1x01_offset]
  12 = Header 1 [package=1x01_offset]
  13 = Header 1 [package=1x01_offset]
  VCC = Header 1 [package=1x01_offset]
  GND = Header 1 [package=1x01_offset]
  RST = Header 1 [package=1x01_offset]
  SIG = Header 1 [package=1x01_offset]
  VCC_2 = Header 1 [package=1x01_offset]
  GND_2 = Header 1 [package=1x01_offset]

nets:
  N1: ATMega328p.RESET, 10k.Pin_0, RST.1
  N2: ATMega328p.D2, SIG.1
  N3: ATMega328p.D3_(PWM), 7SEG.A
  N4: ATMega328p.D4, 7SEG.F
  N5: ATMega328p.VCC, ATMega328p.AVCC, 10k.Pin_1, VCC.1, VCC_2.1
  N6: ATMega328p.GND, GND.1, GND_2.1
  N7: ATMega328p.D5_(PWM), 470.Pin_0
  N8: ATMega328p.D6_(PWM), 470_2.Pin_0
  N9: ATMega328p.D7, 470_3.Pin_0
  N10: ATMega328p.D8, 470_4.Pin_0
  N11: ATMega328p.D9_(PWM), 7SEG.B
  N12: ATMega328p.D10_(PWM), 7SEG.G
  N13: ATMega328p.D11_(PWM), 11.1
  N14: ATMega328p.D12, 12.1
  N15: ATMega328p.D13, 13.1
  N16: ATMega328p.A2, 7SEG.C
  N17: ATMega328p.A3, 7SEG.DOT
  N18: ATMega328p.A4, 7SEG.D
  N19: ATMega328p.A5, 7SEG.E
  N20: 470.Pin_1, 7SEG.D1
  N21: 470_2.Pin_1, 7SEG.D2
  N22: 470_3.Pin_1, 7SEG.D3
  N23: 470_4.Pin_1, 7SEG.D4

custom parts:
  7-SEGMENT-4DIGIT-YOUNGSUN: This is a part for the 4-Digit 7-segment LEDs from Young Sun. Different from the Digikey LEDs, all 16 pins are used. The LONGPADS Variant is used for a test jig, but you may like it because there is more pad to solder to. If you are concerned about routing space, the standard works just fine though.
