# Fritzing sketch DiagramSensor (saved by Fritzing 0.8.7b)
circuit board: 4cm x 3cm
breadboards: 1

parts:
  LM358 = LM358 [package=dip08]
  10k = Resistor [tolerance=±10% resistance=10k package=THT]
  470 = Resistor [tolerance=±5% resistance=470 package=THT]
  10k_2 = Trimmer Potentiometer [maximum_resistance=10kΩ package=THT]
  470_2 = Resistor [tolerance=±5% resistance=470 package=THT]
  LED = LED - 3mm [color="Red (633nm)" package="3 mm [THT]"]
  IR_LED = LED - 3mm [color="Infrared (850nm)" package="3 mm [THT]"]
  IR_PD = LED - 3mm [color="Infrared (850nm)" package="3 mm [THT]"]
  GND = Header 1 [package=1x01_offset]
  VCC = Header 1 [package=1x01_offset]
  SIG = Header 1 [package=1x01_offset]

nets:
  N1: LM358.G$1_OUT, LED.anode, SIG.1
  N2: LM358.G$1_-IN, 10k_2.wiper
  N3: LM358.G$1_+IN, 10k.Pin_0, IR_PD.anode
  GND: LM358.G$1_V-, 10k.Pin_1, 470.Pin_1, 10k_2.leg1, 470_2.Pin_1, GND.1
  5V: LM358.G$1_V+, 10k_2.leg2, IR_LED.anode, IR_PD.cathode, VCC.1
  N4: 470.Pin_0, IR_LED.cathode
  N5: 470_2.Pin_0, LED.cathode
